# Fritzing sketch Schematics (saved by Fritzing 0.9.3b)
breadboards: 1

parts:
  L1 = Solenoid
  Part1 = Arduino Mega 2560 (Rev3)
  U1 = POT [package=pot_mammoth]
  LCD1 = LCD screen
  Part2 = Soil Moisture Sensor
  Part3 = Bluetooth HC-05 Macho
  R1 = Resistor [tolerance=±5% resistance=1k package=THT]
  R2 = Resistor [tolerance=±5% resistance=1k package=THT]
  DS1 = DS18B20 1-Wire Temperature Sensor [part_number=DS18B20]
  Q1 = NPN-Transistor [package="TO92 [THT]"]
  VCC1 = Battery block 9V

nets:
  N1: L1.pin1, VCC1.-
  N2: L1.pin2, Q1.E
  N3: Part1.A0, Part2.SIG
  N4: Part1.A1, DS1.DQ
  N5: Part1.D0_RX0, Part3.TXD
  N6: Part1.D1_TX0, R1.Pin_0, R2.Pin_0
  VDD: Part1.5V, LCD1.VDD, LCD1.LED+, Part2.VCC, Part3.VCC, DS1.VDD
  N7: Part1.D22, LCD1.DB7
  N8: Part1.D24, LCD1.DB6
  N9: Part1.D26, LCD1.DB5
  N10: Part1.D28, LCD1.DB4
  N11: Part1.D30, LCD1.E
  N12: Part1.D32, LCD1.RS
  N13: Part1.D34, Q1.B
  GND: Part1.GND, LCD1.R/W, LCD1.LED-, Part2.GND, Part3.GND, R2.Pin_1, DS1.GND
  N14: U1.S, LCD1.VSS
  N15: U1.A, LCD1.V0
  N16: Part3.RXD, R1.Pin_1
  N17: Q1.C, VCC1.+
